// Logisim project cpu.circ as structural Verilog: 1 circuit, main circuit cpu
module cpu (
  input  clk,
  input  [31:0] Instruction,
  input  [31:0] MemReadData,
  output [31:0] MemAddress,
  output [31:0] ProgramCounter,
  output [31:0] ra,
  output [31:0] sp,
  output [31:0] t0,
  output [31:0] t1,
  output [31:0] t2,
  output [31:0] s0,
  output [31:0] s1,
  output [31:0] a0,
  output [3:0] MemWriteMask,
  output [31:0] MemWriteData
);

  wire ASel, BrEq, BrLt, BrUn, BSel, MemEn, PCSel, RegWEn;
  wire [1:0] WBSel;
  wire [2:0] funct3, ImmSel;
  wire [3:0] ALUSel;
  wire [4:0] rd, rs1, rs2;
  wire [6:0] opcode;
  wire [31:0] A_Value, adder_1_out, B_Value, DataToReg, immedimate, multiplexer_1_out, PCPlus4, PCValue,
       ReadData1, ReadData2, ST2PC, WBData;
  wire [31:25] ST2INS;

  Register #(.width(32)) PC (.D(PCValue), .clk(clk), .Q(ProgramCounter));  // open: en, clr
  Multiplexer #(.width(32)) multiplexer_1 (.in0(Instruction), .in1(32'h13), .out(multiplexer_1_out), .sel(PCSel));
  Adder #(.width(32)) adder_1 (.a(ProgramCounter), .b(32'h4), .out(adder_1_out));  // open: cin, cout
  Register #(.width(32)) register_1 (.D(ProgramCounter), .clk(clk), .Q(ST2PC));  // open: en, clr
  Register #(.width(32)) register_2 (
    .D(multiplexer_1_out), .clk(clk), .Q({ST2INS, rs2, rs1, funct3, rd, opcode}));  // open: en, clr
  Multiplexer #(.width(32)) multiplexer_2 (.in0(adder_1_out), .in1(MemAddress), .out(PCValue), .sel(PCSel));
  control_logic control_logic_1 (
    .Instruction({ST2INS, rs2, rs1, funct3, rd, opcode}), .BrEq(BrEq), .BrLt(BrLt), .PCSel(PCSel),
    .RegWEn(RegWEn), .ImmSel(ImmSel), .BrUn(BrUn), .ASel(ASel), .BSel(BSel), .ALUSel(ALUSel), .MemWEn(MemEn),
    .WBSel(WBSel));
  regfile regfile_1 (
    .ReadIndex1(rs1), .ReadIndex2(rs2), .WriteIndex(rd), .WriteData(WBData), .RegWEn(RegWEn), .clk(clk),
    .ra(ra), .sp(sp), .t0(t0), .t1(t1), .t2(t2), .s0(s0), .s1(s1), .a0(a0), .ReadData1(ReadData1),
    .ReadData2(ReadData2));
  imm_gen imm_gen_1 (.Instruction({ST2INS, rs2, rs1, funct3, rd, opcode}), .ImmSel(ImmSel), .Immediate(immedimate));
  alu alu_1 (.A(A_Value), .B(B_Value), .ALUSel(ALUSel), .ALUResult(MemAddress));
  branch_comp branch_comp_1 (.BrData1(ReadData1), .BrData2(ReadData2), .BrUn(BrUn), .BrEq(BrEq), .BrLt(BrLt));
  Adder #(.width(32)) adder_2 (.a(ST2PC), .b(32'h4), .out(PCPlus4));  // open: cin, cout
  Multiplexer #(.width(32)) multiplexer_3 (.in0(ReadData2), .in1(immedimate), .out(B_Value), .sel(BSel));
  Multiplexer #(.width(32)) multiplexer_4 (.in0(ReadData1), .in1(ST2PC), .out(A_Value), .sel(ASel));
  Multiplexer #(.select(2), .width(32)) multiplexer_5 (
    .in0(DataToReg), .in1(MemAddress), .in2(PCPlus4), .out(WBData), .sel(WBSel));  // open: in3
  partial_store partial_store_1 (
    .Instruction({ST2INS, rs2, rs1, funct3, rd, opcode}), .MemAddress(MemAddress), .DataFromReg(ReadData2),
    .MemWEn(MemEn), .MemWriteMask(MemWriteMask), .DataToMem(MemWriteData));
  partial_load partial_load_1 (
    .Instruction({ST2INS, rs2, rs1, funct3, rd, opcode}), .MemAddress(MemAddress), .DataFromMem(MemReadData),
    .DataToReg(DataToReg));

  // Other names for the same wires on the sheet: ALUResult[31:0] = MemAddress;
  //   ST2INS[24:0] = {rs2, rs1, funct3, rd, opcode}

  // Notes on the sheet:
  //   To IMEM
  //   IMEM (do **NOT** move this)
  //   From IMEM
  //   Inputs/Outputs for testing. Do **NOT** move these.
  //   It is OK to move the PC, RegFile, ALU, MEM, Branch Comp, Imm Gen, Partial Load, Partial Store and Control Logic to wherever is most convenient for you when constructing your CPU, and to delete this text
  //   To DMEM
  //   DMEM (do **NOT** move this)
  //   From DMEM
endmodule
